# Fritzing sketch 1144-modulations-online (saved by Fritzing 0.8.7b)
breadboards: 1

parts:
  C2 = Electrolytic Capacitor [capacitance=1000μF package="1010 [SMD, electrolytic]"]
  Part1 = Audio Jack Breakout
  U1 = 555 Timer [package="SO8 [SMD]"]
  R3 = Resistor [tolerance=±5% resistance=10k package=THT]
  Part2 = Audio Jack Breakout
  C3 = Electrolytic Capacitor [capacitance=100µF package="200 mil [THT, electrolytic]"]
  R4 = Resistor [tolerance=±5% resistance=130k package=THT]
  R5 = Resistor [tolerance=±5% resistance=150k package=THT]
  C4 = Ceramic Capacitor [capacitance=100nF package="100 mil [THT, multilayer]"]
  R6 = Resistor [tolerance=±5% resistance=1k package=THT]
  R2 = Resistor [tolerance=±5% resistance=10k package=THT]
  R1 = Resistor [tolerance=±5% resistance=1k package=THT]
  R7 = Resistor [tolerance=±5% resistance=1k package=THT]
  C5 = Ceramic Capacitor [capacitance=100nF package="100 mil [THT, multilayer]"]
  C6 = Electrolytic Capacitor [capacitance=1000μF package="1010 [SMD, electrolytic]"]
  U2 = 555 Timer [package="SO8 [SMD]"]
  R8 = Resistor [tolerance=±5% resistance=10k package=THT]
  R9 = Resistor [tolerance=±5% resistance=10k package=THT]
  C7 = Ceramic Capacitor [capacitance=100nF package="100 mil [THT, multilayer]"]
  Q1 = NPN-Transistor [package="TO92 [THT]"]
  R11 = Resistor [tolerance=±5% resistance=130k package=THT]
  R12 = Resistor [tolerance=±5% resistance=150k package=THT]
  R13 = Resistor [tolerance=±5% resistance=7.5k package=THT]
  U3 = BNC [package=bnc]  # not connected
  R14 = Resistor [tolerance=±5% resistance=1k package=THT]
  C8 = Electrolytic Capacitor [capacitance=100µF package="200 mil [THT, electrolytic]"]
  R10 = Rotary Potentiometer (Small) [maximum_resistance=100kΩ package=THT]

nets:
  GND: C2.-, Part1.GND, U1.Pin_1, Part2.GND, R5.Pin_1, C6.-, U2.Pin_1, C7.0, R12.Pin_1, R13.Pin_1
  N1: C2.+, U1.Pin_2, U1.Pin_6
  N2: Part1.RING_SHUNT, R14.Pin_0
  N3: Part1.TIP, R1.Pin_0
  N4: U1.Pin_3, C3.+
  N5: U1.Pin_4, U1.Pin_8, R4.Pin_0, R2.Pin_0, U2.Pin_4, U2.Pin_8, R9.Pin_0, R11.Pin_0
  N6: U1.Pin_7, R3.Pin_0
  N7: Part2.RING_SHUNT, R7.Pin_0
  N8: Part2.TIP, R6.Pin_1
  N9: C3.-, R1.Pin_1
  N10: R4.Pin_1, R5.Pin_0, C4.0
  N11: C4.1, R6.Pin_0
  N12: R7.Pin_1, C5.0
  N13: C5.1, Q1.B, R11.Pin_1, R12.Pin_0
  N14: C6.+, R10.leg1
  N15: U2.Pin_2, U2.Pin_6, R10.wiper
  N16: U2.Pin_3, Q1.C
  N17: U2.Pin_7, R8.Pin_0
  N18: C7.1, R10.leg2
  N19: Q1.E, R13.Pin_0, C8.+
  N20: R14.Pin_1, C8.-
